# Fritzing sketch pyroshield (saved by Fritzing 1.0.4)
circuit board: 8.46667cm x 5.64444cm
perfboards: 1

parts:
  M1 = STM32F103C8T6 blue mini board
  M2 = NEO-6M GPS Module [part_number=GY-GPS6MV2]
  A1 = GY-BMP280 Breakout
  M3 = Osoyoo SX1278-ra-02
  M4 = MT3608 Module
  D1 = Rectifier Diode [package="Melf DO-213 AA [SMD]"]
  R4 = Resistor [tolerance=±5% resistance=15k package="0402 [SMD]"]
  R5 = Resistor [tolerance=±5% resistance=10k package="0402 [SMD]"]
  BATT2 = female pin header, 3 pins [form="♀ (female)"]
  Charger = female pin header, 2 pins [form="♀ (female)"]
  DHT22 = male pin header, 3 pins [form="♂ (male)"]
  MTP40F = male pin header, 4 pins [form="♂ (male)"]
  Prog = male pin header, 4 pins [form="♂ (male)"]
  Switch = male pin header, 2 pins [form="♂ (male)"]
  Debug = male pin header, 3 pins [form="♂ (male)"]
  R6 = Resistor [tolerance=±5% resistance=33k package="0402 [SMD]"]
  R7 = Resistor [tolerance=±5% resistance=15k package="0402 [SMD]"]
  R2 = Resistor [tolerance=±5% resistance=33k package="0402 [SMD]"]

nets:
  N1: M1.B12, Debug.pin2
  N2: M1.B14, M3.RST
  N3: M1.B15, M3.DIO0
  N4: M1.A8, M3.NSS
  N5: M1.A9, Prog.pin2
  N6: M1.A10, Prog.pin3
  N7: M1.B3, M3.SCK
  N8: M1.B4, M3.MISO
  N9: M1.B5, M3.MOSI
  N10: M1.B7, DHT22.pin2
  N11: M1.B8, A1.Pin_3
  N12: M1.B9, A1.Pin_4
  N13: M1.5V, M4.pin3
  GND: M1.G, M1.GND, M2.GND, A1.Pin_2, M3.GND, M4.pin4, DHT22.pin3, MTP40F.pin3, Prog.pin1
  3.3V: M1.3.3V, A1.Pin_1, M3.3.3V, R5.Pin_1, DHT22.pin1, Prog.pin4, Debug.pin3
  N14: M1.C14, A1.Pin_5
  N15: M1.C15, A1.Pin_6
  N16: M1.A0, R5.Pin_0, BATT2.pin3
  N17: M1.A1, R4.Pin_0, R2.Pin_1
  N18: M1.A2, MTP40F.pin2
  N19: M1.A3, MTP40F.pin1
  N20: M1.B0, R6.Pin_1, R7.Pin_0
  N21: M1.B10, M2.Rx
  N22: M1.B11, M2.Tx
  N23: M2.Vcc, MTP40F.pin4
  N24: M4.pin1, R4.Pin_1, BATT2.pin1, Charger.pin2, R7.Pin_1
  N25: M4.pin2, Switch.pin1, R2.Pin_0
  N26: D1.cathode, BATT2.pin2, Switch.pin2
  N27: D1.anode, Charger.pin1, R6.Pin_0

custom parts:
  NEO-6M GPS Module: GY-GPS6MV2 NEO-6M GPS Module Module based on U-blox NEO-6M GPS engine, incorporating regulator for 3.3-5V DC input, MS621FE-compatible rechargeable battery for backup and EEPROM for storing configuration settings. Links: NEO-6 series product information page NEO-6 Datasheet
  Osoyoo SX1278-ra-02: Osoyoo Long Distance wireless transceiver Uart LoRa Module.
  MT3608 Module: MT3608 Boost Converter Module Links: Aerosemi MT3608 2A Step Up Converter datasheet
